# Fritzing sketch Cablage Argos (saved by Fritzing 1.0.8)

parts:
  Data_Logger1 = Campbell Scientific CR-1000
  HAL1 = HAL2 ARGOS/SCD Transmitter

nets:
  N1: Data_Logger1.pin46, HAL1.pin9
  N2: Data_Logger1.pin47, HAL1.pin8
  N3: Data_Logger1.pin48, HAL1.pin7
  N4: Data_Logger1.pin_53, HAL1.pin5, HAL1.pin6
  N5: Data_Logger1.pin_54, HAL1.pin2, HAL1.pin3

custom parts:
  Campbell Scientific CR-1000: This is a Fritzing part for the Campbell Scientific CR1000 datalogger. This is a common industrial data acquistion system.
  HAL2 ARGOS/SCD Transmitter: The HAL2 ARGOS/SCD Transmitter used for message transmission towards ARGOS and SCD satellites, manufactured by ELTA around the year 2005.
