# Fritzing sketch Cablage station (saved by Fritzing 1.0.8)
breadboards: 2

parts:
  Data_Logger1 = Campbell Scientific CR-1000
  Composant1 = SDM-SIO1 [package=dip]
  Composant2 = SDM-SIO1 [package=dip]
  Composant3 = SDM-SIO1 [package=dip]
  HAL1 = HAL2 ARGOS/SCD Transmitter
  PTB1 = Vaisala PTB110 Barometer
  V1 = Viator RS232 HART Interface
  T1 = Traco Power 12V/24V
  L2 = Inductor [package="400 mil [THT]"]
  D2 = Rectifier Diode [part_number=1N4001 package="300 mil [THT]"]
  Q2 = NPN-Transistor [package="TO92 [THT]"]
  R2 = Resistor [tolerance=±5% power=0.25W resistance=220 package=THT]
  S2 = Pushbutton [package=THT]
  X1 = DB9 Connector [package=db9]
  J1 = Wago 221-413
  J2 = Wago 221-413
  Subconn_Marégraphe = Camdenboss CTB0158-7 [part_number=CTB0158-7 package=THT]
  Subconn_GPS = Camdenboss CTB0158-7 [part_number=CTB0158-7 package=THT]
  J10 = Wago 221-413
  J11 = Wago 221-415
  J12 = Wago 221-415
  J13 = Wago 221-413
  J14 = Camdenboss CTB0158-2 [part_number=CTB0158-2 package=THT]
  R3 = Resistor [tolerance=±5% power=0.25W resistance=220 package=THT]

nets:
  N1: Data_Logger1.pin1, PTB1.pin5
  N2: Data_Logger1.pin3, PTB1.pin2
  N3: Data_Logger1.pin35, L2.pin_0, D2.cathode, X1.6, J13.Pin_1, J13.Pin_2, J13.Pin_3
  N4: Data_Logger1.pin37, X1.2
  N5: Data_Logger1.pin38, PTB1.pin3, T1.pin2, Subconn_Marégraphe.terminal_1, Subconn_GPS.terminal_3, Subconn_GPS.terminal_4, J10.Pin_1, J10.Pin_2, J10.Pin_3, J11.Pin_1, J11.Pin_2, J11.Pin_3, J11.Pin_4, J11.Pin_5
  +12V: Data_Logger1.pin40, Composant1.+12V, Composant2.+12V, Composant3.+12V
  N6: Data_Logger1.pin41, Composant1.G, Composant2.G, Composant3.G#3
  N7: Data_Logger1.pin42, Composant1.C1, Composant2.C1, Composant3.C1
  N8: Data_Logger1.pin43, Composant1.C2, Composant2.C2, Composant3.C2
  N9: Data_Logger1.pin44, Composant1.C3, Composant2.C3, Composant3.C3
  N10: Data_Logger1.pin45, PTB1.pin1
  N11: Data_Logger1.pin46, HAL1.pin9
  N12: Data_Logger1.pin47, HAL1.pin8
  N13: Data_Logger1.pin48, HAL1.pin7
  N14: Data_Logger1.pin49, R2.Pin_0
  N15: Data_Logger1.pin_53, HAL1.pin5, HAL1.pin6, J2.Pin_1, J2.Pin_2, J2.Pin_3
  N16: Data_Logger1.pin_54, HAL1.pin2, HAL1.pin3, J1.Pin_1, J1.Pin_2, J1.Pin_3
  N17: Composant1.Z, Subconn_Marégraphe.terminal_7
  N18: Composant1.Y, Subconn_Marégraphe.terminal_3
  N19: Composant1.B, Subconn_Marégraphe.terminal_2
  N20: Composant1.A, Subconn_Marégraphe.terminal_6
  N21: Composant2.RX-A, Subconn_GPS.terminal_2
  N22: Composant2.TX-Z, Subconn_GPS.terminal_1
  N23: Composant3.G#5, X1.5
  N24: Composant3.RX-A, X1.8
  N25: Composant3.TX-Z, X1.7
  N26: PTB1.pin4, T1.pin1, Subconn_Marégraphe.terminal_5, Subconn_GPS.terminal_5, J12.Pin_1, J12.Pin_2, J12.Pin_4, J12.Pin_5
  N27: V1.leg0, J14.terminal_1, R3.Pin_0
  N28: V1.leg1, T1.pin3, R3.Pin_1
  N29: T1.pin4, J14.terminal_2
  N30: L2.pin_1, D2.anode, Q2.C
  N31: Q2.E, R2.Pin_1
  N32: Q2.B, S2.leg1
  N33: S2.leg0, Subconn_GPS.terminal_6

notes:
  Connecteur subconn radar
  Connecteur subconn marégraphe
  Connecteur subconn GPS

custom parts:
  Campbell Scientific CR-1000: This is a Fritzing part for the Campbell Scientific CR1000 datalogger. This is a common industrial data acquistion system.
  SDM-SIO1: The SDM-SIO1 is a serial expansion module that allows a data logger to communicate with serial devices that interface using true RS-232, RS-422, or RS-485 signals. Up to fifteen SDM-SIO1 modules may be connected to a single data logger SDM interface. Remote serial devices use industry standard hardware and protocols to connect to the data logger through the SDM-SIO1 interface. When operating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
  HAL2 ARGOS/SCD Transmitter: The HAL2 ARGOS/SCD Transmitter used for message transmission towards ARGOS and SCD satellites, manufactured by ELTA around the year 2005.
  Vaisala PTB110 Barometer: Vaisala BAROCAP Barometer PTB110 is designed both for accurate barometric pressure measurements at room temperature and for general environmental pressure monitoring over a wide temperature range.
  Viator RS232 HART Interface: Interface for communication with HART field devices.
  Wago 221-413: Wago 221-413 3 position splicing connector 12AWG.
  Wago 221-415: Wago 221-415 5 position splicing connector 12AWG.
