# Fritzing sketch Cablage_GPS (saved by Fritzing 1.0.8)
breadboards: 1

parts:
  Data_Logger1 = Campbell Scientific CR-1000
  Composant1 = SDM-SIO1 [package=dip]
  Connecteur_Subconn_GPS = Camdenboss CTB0158-8 [part_number=. package=THT]
  J1 = Wago 221-413
  L1 = Inductor [package="400 mil [THT]"]
  D1 = Rectifier Diode [part_number=1N4001 package="300 mil [THT]"]
  Q1 = NPN-Transistor [package="TO92 [THT]"]
  R1 = Resistor [tolerance=±5% power=0.25W resistance=220 package=THT]
  S1 = Pushbutton [package=THT]
  RE1 = Hexadecimal Rotary Encoder [part_number=APEM-PT65-303 package=THT]  # not connected

nets:
  N1: Data_Logger1.pin37, L1.pin_0, D1.cathode
  N2: Data_Logger1.pin38, Connecteur_Subconn_GPS.terminal_3, Connecteur_Subconn_GPS.terminal_4, J1.Pin_1, J1.Pin_2, J1.Pin_3
  N3: Data_Logger1.pin39, Connecteur_Subconn_GPS.terminal_5
  N4: Data_Logger1.pin40, Composant1.+12V
  N5: Data_Logger1.pin41, Composant1.G
  N6: Data_Logger1.pin42, Composant1.C1
  N7: Data_Logger1.pin43, Composant1.C2
  N8: Data_Logger1.pin44, Composant1.C3
  N9: Data_Logger1.pin49, R1.Pin_0
  N10: Data_Logger1.pin51, Q1.B, S1.leg1
  N11: Composant1.RX-A, Connecteur_Subconn_GPS.terminal_2
  N12: Composant1.TX-Z, Connecteur_Subconn_GPS.terminal_1
  N13: Connecteur_Subconn_GPS.terminal_6, S1.leg0
  N14: L1.pin_1, D1.anode, Q1.C
  N15: Q1.E, R1.Pin_1

notes:
  Masse commutée
  TX GPS
  RX GPS
  Masse
  Alim +12V
  Position 0
  1
  2
  3
  4
  5
  6
  7
  8
  Couleurs de sortie côté GPS

custom parts:
  Campbell Scientific CR-1000: This is a Fritzing part for the Campbell Scientific CR1000 datalogger. This is a common industrial data acquistion system.
  SDM-SIO1: The SDM-SIO1 is a serial expansion module that allows a data logger to communicate with serial devices that interface using true RS-232, RS-422, or RS-485 signals. Up to fifteen SDM-SIO1 modules may be connected to a single data logger SDM interface. Remote serial devices use industry standard hardware and protocols to connect to the data logger through the SDM-SIO1 interface. When operating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
  Wago 221-413: Wago 221-413 3 position splicing connector 12AWG.
