# Fritzing sketch Cablage_baro (saved by Fritzing 1.0.8)

parts:
  Data_Logger1 = Campbell Scientific CR-1000
  PTB1 = Vaisala PTB110 Barometer

nets:
  N1: Data_Logger1.pin1, PTB1.pin5
  N2: Data_Logger1.pin3, PTB1.pin2
  N3: Data_Logger1.pin40, PTB1.pin4
  N4: Data_Logger1.pin41, PTB1.pin3
  N5: Data_Logger1.pin45, PTB1.pin1

custom parts:
  Campbell Scientific CR-1000: This is a Fritzing part for the Campbell Scientific CR1000 datalogger. This is a common industrial data acquistion system.
  Vaisala PTB110 Barometer: Vaisala BAROCAP Barometer PTB110 is designed both for accurate barometric pressure measurements at room temperature and for general environmental pressure monitoring over a wide temperature range.
