# Fritzing sketch Cablage_maregraphe (saved by Fritzing 1.0.8)

parts:
  Composant1 = SDM-SIO1 [package=dip]
  Data_Logger1 = Campbell Scientific CR-1000
  Connecteur_Subconn_Marégraphe = Camdenboss CTB0158-8 [part_number=. package=THT]

nets:
  N1: Composant1.C1, Data_Logger1.pin42
  N2: Composant1.C2, Data_Logger1.pin43
  N3: Composant1.C3, Data_Logger1.pin44
  N4: Composant1.G, Data_Logger1.pin41
  N5: Composant1.Z, Connecteur_Subconn_Marégraphe.terminal_7
  N6: Composant1.Y, Connecteur_Subconn_Marégraphe.terminal_3
  N7: Composant1.B, Connecteur_Subconn_Marégraphe.terminal_2
  N8: Composant1.A, Connecteur_Subconn_Marégraphe.terminal_6
  N9: Data_Logger1.pin38, Connecteur_Subconn_Marégraphe.terminal_1
  N10: Data_Logger1.pin39, Connecteur_Subconn_Marégraphe.terminal_5

notes:
  Ground
  +12V
  Rouge/Noir
  5
  4
  3
  2
  1
  8
  7
  6

custom parts:
  SDM-SIO1: The SDM-SIO1 is a serial expansion module that allows a data logger to communicate with serial devices that interface using true RS-232, RS-422, or RS-485 signals. Up to fifteen SDM-SIO1 modules may be connected to a single data logger SDM interface. Remote serial devices use industry standard hardware and protocols to connect to the data logger through the SDM-SIO1 interface. When operating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
  Campbell Scientific CR-1000: This is a Fritzing part for the Campbell Scientific CR1000 datalogger. This is a common industrial data acquistion system.
