# Fritzing sketch Cablage_radar (saved by Fritzing 1.0.8)
breadboards: 1

parts:
  Data_Logger1 = Campbell Scientific CR-1000
  Composant1 = SDM-SIO1 [package=dip]
  X1 = DB9 Connector [package=db9]
  V1 = Viator RS232 HART Interface
  RE1 = Hexadecimal Rotary Encoder [part_number=APEM-PT65-303 package=THT]  # not connected
  R1 = Resistor [tolerance=±5% power=0.25W resistance=220 package=THT]
  Connecteur_subconn_radar = Camdenboss CTB0158-2 [part_number="1=+ et 2=-" package=THT]
  Traco_Power_12V/24V = Traco Power 12V/24V

nets:
  N1: Data_Logger1.pin35, X1.6
  N2: Data_Logger1.pin37, X1.2
  N3: Data_Logger1.pin38, Traco_Power_12V/24V.pin2
  N4: Data_Logger1.pin39, Traco_Power_12V/24V.pin1
  N5: Data_Logger1.pin40, Composant1.+12V
  N6: Data_Logger1.pin41, Composant1.G#3
  N7: Data_Logger1.pin42, Composant1.C1
  N8: Data_Logger1.pin43, Composant1.C2
  N9: Data_Logger1.pin44, Composant1.C3
  N10: Composant1.G#5, X1.5
  N11: Composant1.RX-A, X1.8
  N12: Composant1.TX-Z, X1.7
  N13: V1.leg0, R1.Pin_0, Traco_Power_12V/24V.pin3
  N14: V1.leg1, R1.Pin_1, Connecteur_subconn_radar.terminal_2
  N15: Connecteur_subconn_radar.terminal_1, Traco_Power_12V/24V.pin4

notes:
  Position 1
  2
  1

custom parts:
  Campbell Scientific CR-1000: This is a Fritzing part for the Campbell Scientific CR1000 datalogger. This is a common industrial data acquistion system.
  SDM-SIO1: The SDM-SIO1 is a serial expansion module that allows a data logger to communicate with serial devices that interface using true RS-232, RS-422, or RS-485 signals. Up to fifteen SDM-SIO1 modules may be connected to a single data logger SDM interface. Remote serial devices use industry standard hardware and protocols to connect to the data logger through the SDM-SIO1 interface. When operating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
  Viator RS232 HART Interface: Interface for communication with HART field devices.
